// Logisim project EP02ANTIGO.circ as structural Verilog: 7 circuits, main circuit Somador 1/2
module main (
  input  A0,
  input  A1,
  input  A2,
  input  A3,
  input  Ci0,
  input  B0,
  input  B1,
  input  B2,
  input  B3,
  output Overflow,
  output Co0
);

  wire displaydecoder_1_p2, displaydecoder_1_p3, displaydecoder_1_p4, displaydecoder_1_p5,
       displaydecoder_1_p6, displaydecoder_1_p7, displaydecoder_1_p8, displaydecoder_2_p2,
       displaydecoder_2_p3, displaydecoder_2_p4, displaydecoder_2_p5, displaydecoder_2_p6,
       displaydecoder_2_p7, displaydecoder_2_p8, displaydecoder_3_p2, displaydecoder_3_p3,
       displaydecoder_3_p4, displaydecoder_3_p5, displaydecoder_3_p6, displaydecoder_3_p7,
       displaydecoder_3_p8;
  wire [3:0] somador_4_1_s0;

  Somador_4 somador_4_1 (
    .A0(A0), .S0(somador_4_1_s0[0]), .A1(A1), .S1(somador_4_1_s0[1]), .A2(A2), .S2(somador_4_1_s0[2]),
    .A3(A3), .S3(somador_4_1_s0[3]), .B0(B0), .B1(B1), .B2(B2), .B3(B3), .Ci0(Ci0), .Co3(Co0),
    .Overflow(Overflow));
  // DisplayDecoder displaydecoder_1: pin names not known; wires that end beside it: {A3, A2, A1, A0}, displaydecoder_1_p2, displaydecoder_1_p3, displaydecoder_1_p4, displaydecoder_1_p5, displaydecoder_1_p6, displaydecoder_1_p7, displaydecoder_1_p8
  // DisplayDecoder displaydecoder_2: pin names not known; wires that end beside it: {B3, B2, B1, B0}, displaydecoder_2_p2, displaydecoder_2_p3, displaydecoder_2_p4, displaydecoder_2_p5, displaydecoder_2_p6, displaydecoder_2_p7, displaydecoder_2_p8
  _7_Segment_Display u_7_segment_display_1 (
    .g(displaydecoder_1_p8), .f(displaydecoder_1_p7), .a(displaydecoder_1_p2), .b(displaydecoder_1_p3),
    .e(displaydecoder_1_p6), .d(displaydecoder_1_p5), .c(displaydecoder_1_p4));  // open: dp
  // DisplayDecoder displaydecoder_3: pin names not known; wires that end beside it: somador_4_1_s0, displaydecoder_3_p2, displaydecoder_3_p3, displaydecoder_3_p4, displaydecoder_3_p5, displaydecoder_3_p6, displaydecoder_3_p7, displaydecoder_3_p8
  _7_Segment_Display u_7_segment_display_2 (
    .g(displaydecoder_2_p8), .f(displaydecoder_2_p7), .a(displaydecoder_2_p2), .b(displaydecoder_2_p3),
    .e(displaydecoder_2_p6), .d(displaydecoder_2_p5), .c(displaydecoder_2_p4));  // open: dp
  _7_Segment_Display u_7_segment_display_3 (
    .g(displaydecoder_3_p8), .f(displaydecoder_3_p7), .a(displaydecoder_3_p2), .b(displaydecoder_3_p3),
    .e(displaydecoder_3_p6), .d(displaydecoder_3_p5), .c(displaydecoder_3_p4));  // open: dp
endmodule

module Somador_1_2 (
  input  A0,
  input  B0,
  output Soma,
  output Carry_Out
);

  xor xor_1 (Soma, A0, B0);
  and and_1 (Carry_Out, A0, B0);
endmodule

module Somador_1 (
  input  A0,
  input  B0,
  input  Ci0,
  output S0,
  output Co0
);

  wire somador_1_2_1_carry_out, somador_1_2_1_soma, somador_1_2_2_carry_out;

  Somador_1_2 somador_1_2_1 (.A0(A0), .B0(B0), .Soma(somador_1_2_1_soma), .Carry_Out(somador_1_2_1_carry_out));
  Somador_1_2 somador_1_2_2 (.A0(somador_1_2_1_soma), .B0(Ci0), .Soma(S0), .Carry_Out(somador_1_2_2_carry_out));
  or or_1 (Co0, somador_1_2_2_carry_out, somador_1_2_1_carry_out);
endmodule

module Somador_4 (
  input  A0,
  input  A1,
  input  A2,
  input  A3,
  input  Ci0,
  input  B0,
  input  B1,
  input  B2,
  input  B3,
  output S0,
  output S1,
  output S2,
  output S3,
  output Co3,
  output Overflow
);

  wire somador_1_1_co0, somador_1_2_co0, somador_1_3_co0;

  Somador_1 somador_1_1 (.A0(A0), .B0(B0), .Ci0(Ci0), .S0(S0), .Co0(somador_1_1_co0));
  Somador_1 somador_1_2 (.A0(A1), .B0(B1), .Ci0(somador_1_1_co0), .S0(S1), .Co0(somador_1_2_co0));
  Somador_1 somador_1_3 (.A0(A2), .B0(B2), .Ci0(somador_1_2_co0), .S0(S2), .Co0(somador_1_3_co0));
  Somador_1 somador_1_4 (.A0(A3), .B0(B3), .Ci0(somador_1_3_co0), .S0(S3), .Co0(Co3));
  xor xor_1 (Overflow, somador_1_3_co0, Co3);
endmodule

module ULA_1Bit (
  input  Carry_in,
  input  A,
  input  B,
  input  Binvert,
  input  Op1,
  input  Op0,
  output Result,
  output Carry_out
);

  wire and_1_out, multiplexer_1_out, not_1_out, not_2_out, or_1_out, somador_1_1_s0;

  Multiplexer #(.enable("false")) multiplexer_1 (.in0(B), .in1(not_1_out), .out(multiplexer_1_out), .sel(Binvert));
  not not_1 (not_1_out, B);
  and and_1 (and_1_out, A, multiplexer_1_out);
  or or_1 (or_1_out, A, multiplexer_1_out);
  not not_2 (not_2_out, A);
  Somador_1 somador_1_1 (.A0(A), .B0(multiplexer_1_out), .Ci0(Carry_in), .S0(somador_1_1_s0), .Co0(Carry_out));
  Multiplexer #(.select(2), .enable("false")) multiplexer_2 (
    .in0(and_1_out), .in1(or_1_out), .in2(not_2_out), .in3(somador_1_1_s0), .out(Result), .sel({Op1, Op0}));

  // Notes on the sheet:
  //   Binvert: pull=up
endmodule

module ULA_4Bit (
  input  B3,
  input  B2,
  input  B1,
  input  B0,
  input  A3,
  input  A2,
  input  A1,
  input  A0,
  input  Binvert,
  input  Op1,
  input  Op0,
  output S0,
  output S1,
  output S2,
  output S3,
  output C_out
);

  wire ula_1bit_1_carry_out, ula_1bit_2_carry_out, ula_1bit_3_carry_out;

  ULA_1Bit ula_1bit_1 (
    .A(A0), .B(B0), .Result(S0), .Binvert(Binvert), .Carry_out(ula_1bit_1_carry_out), .Carry_in(Binvert),
    .Op1(Op1), .Op0(Op0));
  ULA_1Bit ula_1bit_2 (
    .A(A1), .B(B1), .Result(S1), .Binvert(Binvert), .Carry_out(ula_1bit_2_carry_out),
    .Carry_in(ula_1bit_1_carry_out), .Op1(Op1), .Op0(Op0));
  ULA_1Bit ula_1bit_3 (
    .A(A2), .B(B2), .Result(S2), .Binvert(Binvert), .Carry_out(ula_1bit_3_carry_out),
    .Carry_in(ula_1bit_2_carry_out), .Op1(Op1), .Op0(Op0));
  ULA_1Bit ula_1bit_4 (
    .A(A3), .B(B3), .Result(S3), .Binvert(Binvert), .Carry_out(C_out), .Carry_in(ula_1bit_3_carry_out),
    .Op1(Op1), .Op0(Op0));

  // Notes on the sheet:
  //   C_in
  //   C_OUT
  //   C_OUT
  //   C_OUT
endmodule

module ULA_74LS181 (
  input  [3:0] A,
  input  [3:0] B,
  input  [3:0] in_3,
  output [3:0] out_4
);

  wire [3:0] and_1_out, and_2_out, and_3_out, nand_1_out, nor_1_out, not_1_out, not_2_out, not_3_out,
       not_4_out, not_5_out, not_6_out, or_1_out, or_2_out, or_3_out, xnor_1_out, xor_1_out;

  assign not_1_out = ~A;  // NOT_Gate not_1, 4 bits wide
  assign not_2_out = ~B;  // NOT_Gate not_2, 4 bits wide
  assign not_3_out = ~A;  // NOT_Gate not_3, 4 bits wide
  assign not_4_out = ~B;  // NOT_Gate not_4, 4 bits wide
  assign not_5_out = ~A;  // NOT_Gate not_5, 4 bits wide
  assign nor_1_out = ~(A | B);  // NOR_Gate nor_1, 4 bits wide
  assign and_1_out = not_1_out & B;  // AND_Gate and_1, 4 bits wide
  assign nand_1_out = ~(A & B);  // NAND_Gate nand_1, 4 bits wide
  assign not_6_out = ~B;  // NOT_Gate not_6, 4 bits wide
  assign xor_1_out = A ^ B;  // XOR_Gate xor_1, 4 bits wide
  assign and_2_out = A & not_2_out;  // AND_Gate and_2, 4 bits wide
  assign or_1_out = not_3_out | B;  // OR_Gate or_1, 4 bits wide
  assign xnor_1_out = ~(A ^ B);  // XNOR_Gate xnor_1, 4 bits wide
  assign and_3_out = A & B;  // AND_Gate and_3, 4 bits wide
  assign or_2_out = A | not_4_out;  // OR_Gate or_2, 4 bits wide
  assign or_3_out = A | B;  // OR_Gate or_3, 4 bits wide
  Multiplexer #(.select(4), .width(4), .enable("false")) multiplexer_1 (
    .in0(not_5_out), .in1(nor_1_out), .in2(and_1_out), .in3(4'b0000), .in4(nand_1_out), .in5(not_6_out),
    .in6(xor_1_out), .in7(and_2_out), .in8(or_1_out), .in9(xnor_1_out), .in10(B), .in11(and_3_out),
    .in12(4'b1111), .in13(or_2_out), .in14(or_3_out), .in15(A), .out(out_4), .sel(in_3));
endmodule
