// Logisim project pratico.circ as structural Verilog: 8 circuits, main circuit main
module main (
  input  A3,
  input  A2,
  input  A1,
  input  A0,
  input  B3,
  input  B2,
  input  B1,
  input  B0,
  input  Ci,
  output Co
);

  wire decodificador7_1_a, decodificador7_1_b, decodificador7_1_c, decodificador7_1_d, decodificador7_1_e,
       decodificador7_1_f, decodificador7_1_g, decodificador7_2_a, decodificador7_2_b, decodificador7_2_c,
       decodificador7_2_d, decodificador7_2_e, decodificador7_2_f, decodificador7_2_g, decodificador7_3_a,
       decodificador7_3_b, decodificador7_3_c, decodificador7_3_d, decodificador7_3_e, decodificador7_3_f,
       decodificador7_3_g, somador4bits_1_co2, somador4bits_1_flag_negativo, somador4bits_1_flag_zero,
       somador4bits_1_s0, somador4bits_1_s1, somador4bits_1_s2, somador4bits_1_s3, xor_1_out;

  Somador4Bits somador4bits_1 (
    .B1(B1), .A1(A1), .A2(A2), .B2(B2), .A0(A0), .B0(B0), .Ci0(Ci), .A3(A3), .B3(B3), .S3(somador4bits_1_s3),
    .Co3(Co), .flag_negativo(somador4bits_1_flag_negativo), .flag_zero(somador4bits_1_flag_zero),
    .S0(somador4bits_1_s0), .S1(somador4bits_1_s1), .S2(somador4bits_1_s2), .Co2(somador4bits_1_co2));
  LED flag_zero (.in(somador4bits_1_flag_zero));
  LED flag_negativo (.in(somador4bits_1_flag_negativo));
  xor xor_1 (xor_1_out, Co, somador4bits_1_co2);
  Decodificador7 decodificador7_1 (
    .In3(A3), .In2(A2), .In1(A1), .In0(A0), .a(decodificador7_1_a), .b(decodificador7_1_b),
    .c(decodificador7_1_c), .d(decodificador7_1_d), .e(decodificador7_1_e), .f(decodificador7_1_f),
    .g(decodificador7_1_g));
  LED led_1 (.in(xor_1_out));
  Decodificador7 decodificador7_2 (
    .In3(B3), .In2(B2), .In1(B1), .In0(B0), .a(decodificador7_2_a), .b(decodificador7_2_b),
    .c(decodificador7_2_c), .d(decodificador7_2_d), .e(decodificador7_2_e), .f(decodificador7_2_f),
    .g(decodificador7_2_g));
  _7_Segment_Display u_7_segment_display_1 (
    .g(decodificador7_1_g), .f(decodificador7_1_f), .a(decodificador7_1_a), .b(decodificador7_1_b),
    .e(decodificador7_1_e), .d(decodificador7_1_d), .c(decodificador7_1_c));  // open: dp
  _7_Segment_Display u_7_segment_display_2 (
    .g(decodificador7_2_g), .f(decodificador7_2_f), .a(decodificador7_2_a), .b(decodificador7_2_b),
    .e(decodificador7_2_e), .d(decodificador7_2_d), .c(decodificador7_2_c));  // open: dp
  Decodificador7 decodificador7_3 (
    .In3(somador4bits_1_s3), .In2(somador4bits_1_s2), .In1(somador4bits_1_s1), .In0(somador4bits_1_s0),
    .a(decodificador7_3_a), .b(decodificador7_3_b), .c(decodificador7_3_c), .d(decodificador7_3_d),
    .e(decodificador7_3_e), .f(decodificador7_3_f), .g(decodificador7_3_g));
  _7_Segment_Display u_7_segment_display_3 (
    .g(decodificador7_3_g), .f(decodificador7_3_f), .a(decodificador7_3_a), .b(decodificador7_3_b),
    .e(decodificador7_3_e), .d(decodificador7_3_d), .c(decodificador7_3_c));  // open: dp
endmodule

module MeioSomador (
  input  a0,
  input  b0,
  output Soma,
  output CarryOut
);

  xor xor_1 (Soma, a0, b0);
  and and_1 (CarryOut, a0, b0);
endmodule

module SomadorCompleto (
  input  A0,
  input  B0,
  input  Ci0,
  output Co0,
  output S0
);

  wire meiosomador_1_carryout, meiosomador_1_soma, meiosomador_2_carryout;

  MeioSomador meiosomador_1 (.a0(A0), .b0(B0), .Soma(meiosomador_1_soma), .CarryOut(meiosomador_1_carryout));
  MeioSomador meiosomador_2 (.a0(meiosomador_1_soma), .b0(Ci0), .Soma(S0), .CarryOut(meiosomador_2_carryout));
  or or_1 (Co0, meiosomador_1_carryout, meiosomador_2_carryout);
endmodule

module Somador4Bits (
  input  A3,
  input  B3,
  input  A2,
  input  A1,
  input  B2,
  input  B1,
  input  A0,
  input  B0,
  input  Ci0,
  output Co3,
  output Co2,
  output S3,
  output S1,
  output S0,
  output S2,
  output flag_negativo,
  output flag_zero
);

  wire somadorcompleto_1_co0, somadorcompleto_2_co0;

  SomadorCompleto somadorcompleto_1 (.A0(A0), .B0(B0), .Ci0(Ci0), .Co0(somadorcompleto_1_co0), .S0(S0));
  SomadorCompleto somadorcompleto_2 (
    .A0(A1), .B0(B1), .Ci0(somadorcompleto_1_co0), .Co0(somadorcompleto_2_co0), .S0(S1));
  SomadorCompleto somadorcompleto_3 (.A0(A2), .B0(B2), .Ci0(somadorcompleto_2_co0), .Co0(Co2), .S0(S2));
  SomadorCompleto somadorcompleto_4 (.A0(A3), .B0(B3), .Ci0(Co2), .Co0(Co3), .S0(flag_negativo));
  nor nor_1 (flag_zero, S0, S1, flag_negativo);

  assign S3 = flag_negativo;
endmodule

module Decodificador7 (
  input  In3,
  input  In2,
  input  In1,
  input  In0,
  output a,
  output b,
  output c,
  output d,
  output e,
  output f,
  output g
);

  wire and_1_out, and_2_out, and_3_out, and_4_out, and_5_out, and_6_out, and_7_out, and_8_out, and_9_out,
       and_10_out, and_11_out, and_12_out, and_13_out, and_14_out, and_15_out, and_16_out, and_17_out,
       and_18_out, and_19_out, and_20_out, and_21_out, and_22_out, and_23_out, and_24_out, and_25_out,
       and_26_out, and_27_out, and_28_out, and_29_out, and_30_out, and_31_out, and_32_out, and_33_out,
       and_34_out, and_35_out, not_1_out, not_2_out, not_3_out, not_4_out;

  not not_1 (not_1_out, In3);
  not not_2 (not_2_out, In2);
  not not_3 (not_3_out, In1);
  not not_4 (not_4_out, In0);
  and and_1 (and_1_out, not_2_out, not_4_out);
  and and_2 (and_2_out, not_1_out, In1);
  and and_3 (and_3_out, not_1_out, In2, In0);
  and and_4 (and_4_out, In3, not_2_out, not_3_out);
  and and_5 (and_5_out, In3, not_4_out);
  and and_6 (and_6_out, In2, In1);
  and and_7 (and_7_out, not_1_out, not_3_out, not_4_out);
  and and_8 (and_8_out, not_1_out, In1, In0);
  and and_9 (and_9_out, not_2_out, not_4_out);
  and and_10 (and_10_out, In3, not_3_out, In0);
  and and_11 (and_11_out, not_1_out, not_2_out);
  and and_12 (and_12_out, not_1_out, In2);
  and and_13 (and_13_out, In3, not_2_out);
  and and_14 (and_14_out, not_3_out, In0);
  and and_15 (and_15_out, not_2_out, not_3_out);
  and and_16 (and_16_out, not_2_out, In0);
  and and_17 (and_17_out, In2, not_3_out, In0);
  and and_18 (and_18_out, not_1_out, not_2_out, not_4_out);
  and and_19 (and_19_out, not_2_out, In1, In0);
  and and_20 (and_20_out, In3, not_3_out);
  and and_21 (and_21_out, In2, In1, not_4_out);
  and and_22 (and_22_out, not_2_out, not_4_out);
  and and_23 (and_23_out, In1, not_4_out);
  and and_24 (and_24_out, In3, In1);
  and and_25 (and_25_out, In3, In2);
  and and_26 (and_26_out, not_3_out, not_4_out);
  and and_27 (and_27_out, not_1_out, In2, not_3_out);
  and and_28 (and_28_out, In2, not_4_out);
  and and_29 (and_29_out, In3, not_2_out);
  and and_30 (and_30_out, In3, In1);
  and and_31 (and_31_out, not_2_out, In1);
  and and_32 (and_32_out, In3, not_2_out);
  and and_33 (and_33_out, not_1_out, In2, not_3_out);
  and and_34 (and_34_out, In1, not_4_out);
  and and_35 (and_35_out, In3, In0);
  or or_1 (a, and_1_out, and_2_out, and_3_out, and_4_out, and_5_out, and_6_out);
  or or_2 (b, and_7_out, and_8_out, and_9_out, and_10_out, and_11_out);
  or or_3 (c, and_12_out, and_13_out, and_14_out, and_15_out, and_16_out);
  or or_4 (d, and_17_out, and_18_out, and_19_out, and_20_out, and_21_out);
  or or_5 (e, and_22_out, and_23_out, and_24_out, and_25_out);
  or or_6 (f, and_26_out, and_27_out, and_28_out, and_29_out, and_30_out);
  or or_7 (g, and_31_out, and_32_out, and_33_out, and_34_out, and_35_out);
endmodule

module ULA_1bit (
  input  A,
  input  B,
  input  Binvert,
  input  Op1,
  input  Op0,
  input  Carry_in,
  output Result,
  output Carry_out
);

  wire and_1_out, not_1_out, or_1_out, somadorcompleto_1_s0, xor_1_out;

  xor xor_1 (xor_1_out, B, Binvert);
  and and_1 (and_1_out, A, B);
  or or_1 (or_1_out, A, B);
  not not_1 (not_1_out, A);
  SomadorCompleto somadorcompleto_1 (
    .A0(A), .B0(xor_1_out), .Ci0(Carry_in), .Co0(Carry_out), .S0(somadorcompleto_1_s0));
  Multiplexer #(.select(2)) multiplexer_1 (
    .in0(and_1_out), .in1(or_1_out), .in2(not_1_out), .in3(somadorcompleto_1_s0), .out(Result),
    .sel({Op0, Op1}));
endmodule

module ULA_4bits (
  input  binvert,
  input  b3,
  input  b2,
  input  b1,
  input  b0,
  input  a3,
  input  a2,
  input  a1,
  input  a0,
  input  op1,
  input  op0,
  output S0,
  output S1,
  output S2,
  output S3,
  output Cout
);

  wire ula_1bit_1_carry_out, ula_1bit_2_carry_out, ula_1bit_3_carry_out;

  ULA_1bit ula_1bit_1 (
    .A(a0), .B(b0), .Binvert(binvert), .Op1(op1), .Op0(op0), .Carry_in(binvert), .Result(S0),
    .Carry_out(ula_1bit_1_carry_out));
  ULA_1bit ula_1bit_2 (
    .A(a1), .B(b1), .Binvert(binvert), .Op1(op1), .Op0(op0), .Carry_in(ula_1bit_1_carry_out), .Result(S1),
    .Carry_out(ula_1bit_2_carry_out));
  ULA_1bit ula_1bit_3 (
    .A(a2), .B(b2), .Binvert(binvert), .Op1(op1), .Op0(op0), .Carry_in(ula_1bit_2_carry_out), .Result(S2),
    .Carry_out(ula_1bit_3_carry_out));
  ULA_1bit ula_1bit_4 (
    .A(a3), .B(b3), .Binvert(binvert), .Op1(op1), .Op0(op0), .Carry_in(ula_1bit_3_carry_out), .Result(S3),
    .Carry_out(Cout));
endmodule

module Parte2ex2 (
  input  [3:0] B,
  input  [3:0] A,
  input  [3:0] S,
  output [3:0] F
);

  wire [3:0] and_1_out, and_2_out, and_3_out, nand_1_out, nor_1_out, not_1_out, not_2_out, not_3_out,
       not_4_out, not_5_out, not_6_out, or_1_out, or_2_out, or_3_out, xnor_1_out, xor_1_out;

  assign not_1_out = ~A;  // NOT_Gate not_1, 4 bits wide
  assign nor_1_out = ~(A | B);  // NOR_Gate nor_1, 4 bits wide
  assign not_2_out = ~A;  // NOT_Gate not_2, 4 bits wide
  assign not_3_out = ~B;  // NOT_Gate not_3, 4 bits wide
  assign not_4_out = ~B;  // NOT_Gate not_4, 4 bits wide
  assign not_5_out = ~A;  // NOT_Gate not_5, 4 bits wide
  assign not_6_out = ~B;  // NOT_Gate not_6, 4 bits wide
  assign and_1_out = not_2_out & B;  // AND_Gate and_1, 4 bits wide
  assign nand_1_out = ~(A & B);  // NAND_Gate nand_1, 4 bits wide
  assign xor_1_out = A ^ B;  // XOR_Gate xor_1, 4 bits wide
  assign and_2_out = A & not_4_out;  // AND_Gate and_2, 4 bits wide
  assign or_1_out = not_5_out | B;  // OR_Gate or_1, 4 bits wide
  assign xnor_1_out = ~(A ^ B);  // XNOR_Gate xnor_1, 4 bits wide
  assign and_3_out = A & B;  // AND_Gate and_3, 4 bits wide
  assign or_2_out = A | not_6_out;  // OR_Gate or_2, 4 bits wide
  assign or_3_out = A | B;  // OR_Gate or_3, 4 bits wide
  Multiplexer #(.select(4), .width(4)) multiplexer_1 (
    .in0(not_1_out), .in1(nor_1_out), .in2(and_1_out), .in3(4'b0000), .in4(nand_1_out), .in5(not_3_out),
    .in6(xor_1_out), .in7(and_2_out), .in8(or_1_out), .in9(xnor_1_out), .in10(B), .in11(and_3_out),
    .in12(4'b1111), .in13(or_2_out), .in14(or_3_out), .in15(A), .out(F), .sel(S));
endmodule
